# Fritzing sketch hyperpan (saved by Fritzing 0.9.2b)

parts:
  R1 = Resistor [tolerance=±5% resistance=330 package="0603 [SMD]"]
  S_opto = TLP621 [package=THT]
  R2 = Resistor [tolerance=±5% resistance=330 package="0603 [SMD]"]
  Focus = smd LED [color="Green (560nm)" package="1206 [SMD]"]
  Shutter = smd LED [color="Red (633nm)" package="1206 [SMD]"]
  Alerts = smd LED [color="Red (633nm)" package="1206 [SMD]"]
  F_opto = TLP621 [package=THT]
  R3 = Resistor [tolerance=±5% resistance=330 package="0603 [SMD]"]
  PermaProto = Adafruit Perma-Proto HAT [part_number="Adafruit #2314 and #2310"]
  Trigger_Connector = female pin header, 3 pins [form="♀ (female)"]
  theta = Pololu DRV 8825 Stepper Motor Carrier, High Current [package=SO16]
  phi = Pololu DRV 8825 Stepper Motor Carrier, High Current [package=SO16]
  C1 = Electrolytic Capacitor [capacitance=100µF voltage=16V package="100 mil [THT, electrolytic]"]
  C2 = Electrolytic Capacitor [capacitance=100µF voltage=16V package="100 mil [THT, electrolytic]"]
  theta_motor = female pin header, 4 pins [form="♀ (female)"]
  phi_motor = female pin header, 4 pins [form="♀ (female)"]
  5V_8A = Power plug
  R4 = Resistor [tolerance=±5% resistance=330 package="0603 [SMD]"]
  R5 = Resistor [tolerance=±5% resistance=330 package="0603 [SMD]"]
  led_1 = smd LED [color="Green (560nm)" package="1206 [SMD]"]
  led_2 = smd LED [color="Green (560nm)" package="1206 [SMD]"]
  M1 = Stepper Motor - Bipolar
  J1 = male pin header, 4 pins [form="♂ (male)"]
  M2 = Stepper Motor - Bipolar
  J2 = male pin header, 4 pins [form="♂ (male)"]

nets:
  N1: R1.Pin_0, PermaProto.GPIO21
  N2: R1.Pin_1, Alerts.anode
  N3: S_opto.Pin_1, PermaProto.GPIO17
  N4: S_opto.Pin_2, Shutter.anode
  N5: S_opto.Pin_4, F_opto.Pin_4, Trigger_Connector.pin2
  N6: S_opto.Pin_3, Trigger_Connector.pin1
  N7: R2.Pin_0, Shutter.cathode
  N8: R2.Pin_1, Alerts.cathode, R3.Pin_1, PermaProto.GND, theta.GND#8, led_1.cathode
  N9: Focus.cathode, R3.Pin_0
  N10: Focus.anode, F_opto.Pin_2
  N11: F_opto.Pin_1, PermaProto.GPIO4
  N12: F_opto.Pin_3, Trigger_Connector.pin3
  N13: PermaProto.GPIO27, theta.STEP
  N14: PermaProto.GPIO22, theta.SLEEP
  N15: PermaProto.GPIO5, phi.DIR
  N16: PermaProto.GPIO6, phi.STEP
  N17: PermaProto.GPIO12, phi.SLEEP
  N18: PermaProto.GPIO16, phi.MS1
  N19: PermaProto.GPIO18, theta.DIR
  N20: PermaProto.GPIO23, theta.MS2
  N21: PermaProto.GPIO24, theta.MS1
  N22: PermaProto.GPIO13, phi.MS2
  N23: theta.FAULT, R4.Pin_1
  N24: theta.1B, theta_motor.pin4
  N25: theta.1A, theta_motor.pin3
  N26: theta.2A, theta_motor.pin2
  N27: theta.2B, theta_motor.pin1
  N28: theta.GND#14, phi.GND#14, C1.-, C2.-, 5V_8A.GND
  N29: theta.VMOT, phi.VMOT, C1.+, C2.+, 5V_8A.VCC
  N30: phi.GND#8, R4.Pin_0, led_1.anode, led_2.cathode
  N31: phi.FAULT, R5.Pin_1
  N32: phi.1B, phi_motor.pin4
  N33: phi.1A, phi_motor.pin3
  N34: phi.2A, phi_motor.pin2
  N35: phi.2B, phi_motor.pin1
  N36: R5.Pin_0, led_2.anode
  N37: M1.A, J1.pin4
  N38: M1.C, J1.pin3
  N39: M1.B, J1.pin2
  N40: M1.D, J1.pin1
  N41: M2.A, J2.pin4
  N42: M2.C, J2.pin3
  N43: M2.B, J2.pin2
  N44: M2.D, J2.pin1

custom parts:
  Adafruit Perma-Proto HAT: To kick off the Adafruit HAT party, we have this Perma-Proto inspired plug in daughter board. It has a grid of 0.1" prototyping soldering holes for attaching chips, resistors, LED, potentiometers and more. The holes are connected underneath with traces to mimic the solderless breadboards you're familiar. There's also long power strips for +3V, +5V and Ground connections to the Pi. Near the top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
  Pololu DRV 8825 Stepper Motor Carrier, High Current: DRV 8825 This is a Stepper Motor Controller for integrated circuits. This breakout board for TI’s DRV8825 microstepping bipolar stepper motor driver features adjustable current limiting, over-current and over-temperature protection, and six microstep resolutions (down to 1/32-step). It operates from 8.2 V to 45 V and can deliver up to approximately 1.5 A per phase without a heat sink or forced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
